# Fritzing sketch Science Car Tracker Wiring Diagram (saved by Fritzing 0.9.4)

parts:
  Part2 = Adafruit Gemma M0 [part_number="Adafruit #3501"]
  Part1 = Lithium Ion Polymer Battery 3.7v 100mAh [part_number=1570]  # not connected
  3-pins_Hall_Effect_Sensor1 = mystery part, 3 pins [chip_label="Hall Effect Sensor"]
  S2 = Pushbutton [package="[SMD]"]

nets:
  N1: Part2.3.3V, 3-pins_Hall_Effect_Sensor1.pin1
  N2: Part2.D0_SDA_TX, 3-pins_Hall_Effect_Sensor1.pin3
  N3: Part2.D1_A0, S2.Pin_1, S2.Pin_2
  N4: Part2.GND, 3-pins_Hall_Effect_Sensor1.pin2, S2.Pin_3, S2.Pin_4

notes:
  Science Car Tracker Data Logger
  Wiring Diagram

custom parts:
  Adafruit Gemma M0: The Adafruit Gemma M0 is a super small microcontroller board, with just enough built-in to create many simple projects. It may look small and cute: round, about the size of a quarter, with friendly alligator-clip sew pads. But do not be fooled! The Gemma M0 is incredibly powerful! We've taken the same form factor we used for the original ATtiny85-based Gemma and gave it an upgrade. The Gemma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
  Lithium Ion Polymer Battery 3.7v 100mAh: Lithium ion polymer (also known as 'lipo' or 'lipoly') batteries are thin, light and powerful. The output ranges from 4.2V when completely charged to 3.7V. This battery has a capacity of ~100mAh for a total of about 0.4 Wh. The batteries come pre-attached with a genuine 2-pin JST-PH connector as shown and include the necessary protection circuitry.
